// Logisim project Kolo1.circ as structural Verilog: 1 circuit, main circuit main
module main (
  input  in_1,
  input  in_2,
  output out_3
);

  wire and_1_out, and_2_out, and_3_out, nor_1_out, not_1_out, not_2_out, not_3_out, not_4_out, or_1_out;

  not not_1 (not_1_out, in_1);
  not not_2 (not_2_out, in_1);
  not not_3 (not_3_out, in_1);
  and and_1 (and_1_out, not_1_out, in_2);
  and and_2 (and_2_out, not_2_out, in_2);
  and and_3 (and_3_out, not_3_out, in_2);
  not not_4 (not_4_out, and_2_out);
  or or_1 (or_1_out, and_1_out, and_2_out);
  nor nor_1 (nor_1_out, not_4_out, and_3_out);
  or or_2 (out_3, or_1_out, nor_1_out);
endmodule
