// Logisim project NI.circ as structural Verilog: 3 circuits, main circuit main
module main (
  input  in_1,
  input  in_2,
  input  in_3,
  input  in_4,
  input  in_5,
  output out_6
);
endmodule

module NI_kolo (
  input  a,
  input  b,
  input  c,
  input  d,
  input  e,
  output x
);

  wire nand_1_out, nand_2_out, nand_3_out, nand_4_out, nand_5_out, nand_6_out, nand_7_out, nand_8_out,
       nand_9_out, nand_10_out, nand_11_out;

  nand nand_1 (nand_1_out, b, b);
  nand nand_2 (nand_2_out, a, nand_1_out);
  nand nand_3 (nand_3_out, nand_2_out, nand_2_out);
  nand nand_4 (nand_4_out, c, c);
  nand nand_5 (nand_5_out, d, d);
  nand nand_6 (nand_6_out, e, e);
  nand nand_7 (nand_7_out, nand_3_out, nand_4_out);
  nand nand_8 (nand_8_out, nand_5_out, nand_6_out);
  nand nand_9 (nand_9_out, nand_7_out, nand_7_out);
  nand nand_10 (nand_10_out, nand_8_out, nand_8_out);
  nand nand_11 (nand_11_out, nand_9_out, nand_10_out);
  nand nand_12 (x, nand_11_out, nand_11_out);

  // Notes on the sheet:
  //   16.9
endmodule

module NILI_kolo (
  input  in_1,
  input  in_2,
  input  in_3,
  input  in_4,
  input  in_5
);
endmodule
